// Logisim project ALU.circ as structural Verilog: 14 circuits, main circuit FA-xmx077
module FA_xmx077 (
  input  Ai,
  input  Bi,
  input  Ci,
  output Fi,
  output Ci_1
);

  wire and_1_out, and_2_out, and_3_out;

  xor xor_1 (Fi, Ai, Bi, Ci);
  and and_1 (and_1_out, Bi, Ai);
  and and_2 (and_2_out, Ci, Bi);
  and and_3 (and_3_out, Ci, Ai);
  or or_1 (Ci_1, and_1_out, and_2_out, and_3_out);
endmodule

module GP_xmx077 (
  input  Y0,
  input  X0,
  input  Y1,
  input  X1,
  input  Y2,
  input  X2,
  input  Y3,
  input  X3,
  output G0,
  output P0,
  output G1,
  output P1,
  output G2,
  output P2,
  output G3,
  output P3
);

  and and_1 (G0, Y0, X0);
  or or_1 (P0, Y0, X0);
  and and_2 (G1, Y1, X1);
  or or_2 (P1, Y1, X1);
  and and_3 (G2, Y2, X2);
  or or_3 (P2, Y2, X2);
  and and_4 (G3, Y3, X3);
  or or_4 (P3, Y3, X3);
endmodule

module _4_BIT_CARRY_AHEAD_xmx077 (
  input  G0,
  input  P0,
  input  C0,
  input  G1,
  input  P1,
  input  G2,
  input  P2,
  input  G3,
  input  P3,
  output P_star,
  output C1,
  output C2,
  output C3,
  output G_star,
  output C4
);

  wire and_1_out, and_2_out, and_3_out, and_4_out, and_5_out, and_6_out, and_7_out, and_9_out, and_10_out,
       and_11_out;

  and and_1 (and_1_out, G2, P3);
  and and_2 (and_2_out, P0, C0);
  and and_3 (and_3_out, G0, P1);
  and and_4 (and_4_out, G1, P2);
  and and_5 (and_5_out, and_3_out, P3);
  and and_6 (and_6_out, and_4_out, P3);
  or or_1 (C1, G0, and_2_out);
  and and_7 (and_7_out, and_2_out, P1);
  and and_8 (P_star, P2, P3, P1, P0);
  and and_9 (and_9_out, and_7_out, P2);
  and and_10 (and_10_out, and_5_out, P3);
  or or_2 (C2, G1, and_3_out, and_7_out);
  or or_3 (C3, G2, and_4_out, and_5_out, and_9_out);
  and and_11 (and_11_out, and_9_out, P3);
  or or_4 (G_star, G3, and_1_out, and_6_out, and_10_out);
  or or_5 (C4, G3, and_1_out, and_6_out, and_10_out, and_11_out);
endmodule

module FA_4bits_unsigned_xmx077 (
  input  [3:0] X,
  input  [3:0] Y,
  input  C_in,
  output C3,
  output [3:0] F,
  output OF,
  output CF,
  output G,
  output P
);

  wire C1, C2, gp_xmx077_1_g0, gp_xmx077_1_g1, gp_xmx077_1_g2, gp_xmx077_1_g3, gp_xmx077_1_p0,
       gp_xmx077_1_p1, gp_xmx077_1_p2, gp_xmx077_1_p3;

  GP_xmx077 gp_xmx077_1 (
    .Y0(Y[0]), .X0(X[0]), .Y1(Y[1]), .X1(X[1]), .Y2(Y[2]), .X2(X[2]), .Y3(Y[3]), .X3(X[3]),
    .G0(gp_xmx077_1_g0), .P0(gp_xmx077_1_p0), .G1(gp_xmx077_1_g1), .P1(gp_xmx077_1_p1), .G2(gp_xmx077_1_g2),
    .P2(gp_xmx077_1_p2), .G3(gp_xmx077_1_g3), .P3(gp_xmx077_1_p3));
  xor xor_1 (OF, C3, CF);
  _4_BIT_CARRY_AHEAD_xmx077 u_4_bit_carry_ahead_xmx077_1 (
    .G0(gp_xmx077_1_g0), .P0(gp_xmx077_1_p0), .C0(C_in), .G1(gp_xmx077_1_g1), .P1(gp_xmx077_1_p1),
    .G2(gp_xmx077_1_g2), .P2(gp_xmx077_1_p2), .G3(gp_xmx077_1_g3), .P3(gp_xmx077_1_p3), .P_star(P), .C1(C1),
    .C2(C2), .C3(C3), .G_star(G), .C4(CF));
  FA_xmx077 FA0 (.Ai(X[0]), .Bi(Y[0]), .Ci(C_in), .Fi(F[0]));  // open: Ci_1
  FA_xmx077 FA1 (.Ai(X[1]), .Bi(Y[1]), .Ci(C1), .Fi(F[1]));  // open: Ci_1
  FA_xmx077 FA2 (.Ai(X[2]), .Bi(Y[2]), .Ci(C2), .Fi(F[2]));  // open: Ci_1
  FA_xmx077 FA3 (.Ai(X[3]), .Bi(Y[3]), .Ci(C3), .Fi(F[3]));  // open: Ci_1

  // Other names for the same wires on the sheet: C0 = C_in; C4 = CF
endmodule

module FA_8bits_unsigned_xmx077 (
  input  [7:0] A,
  input  [7:0] B,
  output [7:0] S_A,
  output out_4,
  output out_5
);

  wire fa_4bits_unsigned_xmx077_1_g, fa_4bits_unsigned_xmx077_1_p, fa_4bits_unsigned_xmx077_2_g,
       fa_4bits_unsigned_xmx077_2_p, n4_bit_carry_ahead_xmx077_1_c1;

  FA_4bits_unsigned_xmx077 fa_4bits_unsigned_xmx077_1 (
    .X(A[3:0]), .Y(B[3:0]), .C_in(1'b0), .G(fa_4bits_unsigned_xmx077_1_g), .P(fa_4bits_unsigned_xmx077_1_p),
    .F(S_A[3:0]));  // open: OF, CF, C3
  FA_4bits_unsigned_xmx077 fa_4bits_unsigned_xmx077_2 (
    .X(A[7:4]), .Y(B[7:4]), .C_in(n4_bit_carry_ahead_xmx077_1_c1), .OF(out_4), .CF(out_5),
    .G(fa_4bits_unsigned_xmx077_2_g), .P(fa_4bits_unsigned_xmx077_2_p), .F(S_A[7:4]));  // open: C3
  _4_BIT_CARRY_AHEAD_xmx077 u_4_bit_carry_ahead_xmx077_1 (
    .G0(fa_4bits_unsigned_xmx077_1_g), .P0(fa_4bits_unsigned_xmx077_1_p), .C0(1'b0),
    .G1(fa_4bits_unsigned_xmx077_2_g), .P1(fa_4bits_unsigned_xmx077_2_p), .G2(1'b0), .P2(1'b0), .G3(1'b0),
    .P3(1'b0), .C1(n4_bit_carry_ahead_xmx077_1_c1));  // open: P_star, C2, C3, G_star, C4

  // Other names for the same wires on the sheet: A0_3[3:0] = A[3:0]; A4_7[3:0] = A[7:4]; B0_3[3:0] = B[3:0];
  //   B4_7[3:0] = B[7:4]
endmodule

module FS_1bit_unsigned_xmx077 (
  input  Ai,
  input  Bi,
  input  B_in,
  output F,
  output B_out
);

  wire and_1_out, and_2_out, not_1_out, or_1_out;

  not not_1 (not_1_out, Ai);
  ExactlyOne xor_1 (.out(F), .in0(Ai), .in1(Bi), .in2(B_in));
  and and_1 (and_1_out, not_1_out, Bi);
  or or_1 (or_1_out, not_1_out, Bi);
  and and_2 (and_2_out, or_1_out, B_in);
  or or_2 (B_out, and_1_out, and_2_out);
endmodule

module GP_FS_xmx077 (
  input  Y0,
  input  X0,
  input  Y1,
  input  X1,
  input  Y2,
  input  X2,
  input  Y3,
  input  X3,
  output G0,
  output P0,
  output G1,
  output P1,
  output G2,
  output P2,
  output G3,
  output P3
);

  wire not_1_out, not_2_out, not_3_out, not_4_out;

  not not_1 (not_1_out, Y0);
  not not_2 (not_2_out, Y1);
  not not_3 (not_3_out, Y2);
  not not_4 (not_4_out, Y3);
  and and_1 (G0, not_1_out, X0);
  or or_1 (P0, not_1_out, X0);
  and and_2 (G1, not_2_out, X1);
  or or_2 (P1, not_2_out, X1);
  and and_3 (G2, not_3_out, X2);
  or or_3 (P2, not_3_out, X2);
  and and_4 (G3, not_4_out, X3);
  or or_4 (P3, not_4_out, X3);
endmodule

module FA_8bits_signed_xmx077 (
  input  [7:0] A,
  input  [7:0] B,
  output [7:0] S_A,
  output OF
);

  wire F0_3_g, F0_3_p, F4_7_c3, F4_7_cf, F4_7_g, F4_7_p, n4_bit_carry_ahead_xmx077_1_c1;

  // Probe on A
  // Probe on B
  FA_4bits_unsigned_xmx077 F0_3 (
    .X(A[3:0]), .Y(B[3:0]), .C_in(1'b0), .G(F0_3_g), .P(F0_3_p), .F(S_A[3:0]));  // open: OF, CF, C3
  FA_4bits_unsigned_xmx077 F4_7 (
    .X(A[7:4]), .Y(B[7:4]), .C_in(n4_bit_carry_ahead_xmx077_1_c1), .CF(F4_7_cf), .G(F4_7_g), .P(F4_7_p),
    .F(S_A[7:4]), .C3(F4_7_c3));  // open: OF
  _4_BIT_CARRY_AHEAD_xmx077 u_4_bit_carry_ahead_xmx077_1 (
    .G0(F0_3_g), .P0(F0_3_p), .C0(1'b0), .G1(F4_7_g), .P1(F4_7_p), .G2(1'b0), .P2(1'b0), .G3(1'b0),
    .P3(1'b0), .C1(n4_bit_carry_ahead_xmx077_1_c1));  // open: P_star, C2, C3, G_star, C4
  xor xor_1 (OF, F4_7_c3, F4_7_cf);
  // Probe on S_A

  // Other names for the same wires on the sheet: A0_3[3:0] = A[3:0]; A4_7[3:0] = A[7:4]; B0_3[3:0] = B[3:0];
  //   B4_7[3:0] = B[7:4]
endmodule

module AND_unit_xmx077 (
  input  [3:0] A4,
  input  b,
  output A0b,
  output A1b,
  output A2b,
  output A3b
);

  and and_1 (A0b, A4[0], b);
  and and_2 (A1b, b, A4[1]);
  and and_3 (A2b, A4[2], b);
  and and_4 (A3b, A4[3], b);
endmodule

module MULTIPLY_4bits_xmx077 (
  input  [3:0] B,
  input  [3:0] A,
  output [7:0] F
);

  wire A0b1, A0b2, A0b3, A1b0, A1b1, A1b2, A1b3, A2b0, A2b1, A2b2, A2b3, A3b0, A3b1, A3b2, A3b3, FA10_ci_1,
       FA11_ci_1, FA11_fi, FA12_ci_1, FA12_fi, fa_xmx077_2_ci_1, fa_xmx077_3_ci_1, fa_xmx077_3_fi,
       fa_xmx077_4_ci_1, fa_xmx077_4_fi, fa_xmx077_5_ci_1, fa_xmx077_5_fi, fa_xmx077_6_ci_1,
       fa_xmx077_7_ci_1, fa_xmx077_7_fi, fa_xmx077_8_ci_1, fa_xmx077_9_ci_1;

  // Probe on B
  // Probe on A
  AND_unit_xmx077 b0 (.A4(A), .b(B[0]), .A0b(F[0]), .A1b(A1b0), .A2b(A2b0), .A3b(A3b0));
  AND_unit_xmx077 b1 (.A4(A), .b(B[1]), .A0b(A0b1), .A1b(A1b1), .A2b(A2b1), .A3b(A3b1));
  AND_unit_xmx077 b2 (.A4(A), .b(B[2]), .A0b(A0b2), .A1b(A1b2), .A2b(A2b2), .A3b(A3b2));
  AND_unit_xmx077 b3 (.A4(A), .b(B[3]), .A0b(A0b3), .A1b(A1b3), .A2b(A2b3), .A3b(A3b3));
  FA_xmx077 fa_xmx077_1 (.Ai(A3b3), .Bi(fa_xmx077_2_ci_1), .Ci(fa_xmx077_3_ci_1), .Fi(F[6]), .Ci_1(F[7]));
  FA_xmx077 fa_xmx077_2 (
    .Ai(fa_xmx077_3_fi), .Bi(fa_xmx077_6_ci_1), .Ci(fa_xmx077_5_ci_1), .Fi(F[5]), .Ci_1(fa_xmx077_2_ci_1));
  FA_xmx077 fa_xmx077_3 (.Ai(A3b2), .Bi(A2b3), .Ci(fa_xmx077_4_ci_1), .Fi(fa_xmx077_3_fi), .Ci_1(fa_xmx077_3_ci_1));
  FA_xmx077 fa_xmx077_4 (.Ai(A3b1), .Bi(A2b2), .Ci(FA12_ci_1), .Fi(fa_xmx077_4_fi), .Ci_1(fa_xmx077_4_ci_1));
  FA_xmx077 fa_xmx077_5 (
    .Ai(fa_xmx077_4_fi), .Bi(A1b3), .Ci(fa_xmx077_7_ci_1), .Fi(fa_xmx077_5_fi), .Ci_1(fa_xmx077_5_ci_1));
  FA_xmx077 fa_xmx077_6 (.Ai(fa_xmx077_5_fi), .Bi(1'b0), .Ci(fa_xmx077_8_ci_1), .Fi(F[4]), .Ci_1(fa_xmx077_6_ci_1));
  FA_xmx077 FA12 (.Ai(A3b0), .Bi(A2b1), .Ci(1'b0), .Fi(FA12_fi), .Ci_1(FA12_ci_1));
  FA_xmx077 fa_xmx077_7 (.Ai(FA12_fi), .Bi(A1b2), .Ci(FA11_ci_1), .Fi(fa_xmx077_7_fi), .Ci_1(fa_xmx077_7_ci_1));
  FA_xmx077 fa_xmx077_8 (.Ai(fa_xmx077_7_fi), .Bi(A0b3), .Ci(fa_xmx077_9_ci_1), .Fi(F[3]), .Ci_1(fa_xmx077_8_ci_1));
  FA_xmx077 FA11 (.Ai(A2b0), .Bi(A1b1), .Ci(1'b0), .Fi(FA11_fi), .Ci_1(FA11_ci_1));
  FA_xmx077 fa_xmx077_9 (.Ai(FA11_fi), .Bi(A0b2), .Ci(FA10_ci_1), .Fi(F[2]), .Ci_1(fa_xmx077_9_ci_1));
  // Probe on F
  FA_xmx077 FA10 (.Ai(A1b0), .Bi(A0b1), .Ci(1'b0), .Fi(F[1]), .Ci_1(FA10_ci_1));

  // Other names for the same wires on the sheet: A0b0 = F[0]
endmodule

module FS_4bits_unsigned (
  input  [3:0] Ai,
  input  [3:0] Bi,
  input  B_in,
  output P_star,
  output G_star,
  output B_out,
  output [3:0] S_out
);

  wire C1, C2, C3, gp_fs_xmx077_1_g0, gp_fs_xmx077_1_g1, gp_fs_xmx077_1_g2, gp_fs_xmx077_1_g3,
       gp_fs_xmx077_1_p0, gp_fs_xmx077_1_p1, gp_fs_xmx077_1_p2, gp_fs_xmx077_1_p3;

  FS_1bit_unsigned_xmx077 fs_1bit_unsigned_xmx077_1 (.Ai(Ai[0]), .Bi(Bi[0]), .B_in(B_in), .F(S_out[0]));  // open: B_out
  FS_1bit_unsigned_xmx077 fs_1bit_unsigned_xmx077_2 (.Ai(Ai[1]), .Bi(Bi[1]), .B_in(C1), .F(S_out[1]));  // open: B_out
  GP_FS_xmx077 gp_fs_xmx077_1 (
    .Y0(Ai[0]), .X0(Bi[0]), .Y1(Ai[1]), .X1(Bi[1]), .Y2(Ai[2]), .X2(Bi[2]), .Y3(Ai[3]), .X3(Bi[3]),
    .G0(gp_fs_xmx077_1_g0), .P0(gp_fs_xmx077_1_p0), .G1(gp_fs_xmx077_1_g1), .P1(gp_fs_xmx077_1_p1),
    .G2(gp_fs_xmx077_1_g2), .P2(gp_fs_xmx077_1_p2), .G3(gp_fs_xmx077_1_g3), .P3(gp_fs_xmx077_1_p3));
  FS_1bit_unsigned_xmx077 fs_1bit_unsigned_xmx077_3 (.Ai(Ai[2]), .Bi(Bi[2]), .B_in(C2), .F(S_out[2]));  // open: B_out
  FS_1bit_unsigned_xmx077 fs_1bit_unsigned_xmx077_4 (.Ai(Ai[3]), .Bi(Bi[3]), .B_in(C3), .F(S_out[3]));  // open: B_out
  _4_BIT_CARRY_AHEAD_xmx077 u_4_bit_carry_ahead_xmx077_1 (
    .G0(gp_fs_xmx077_1_g0), .P0(gp_fs_xmx077_1_p0), .C0(B_in), .G1(gp_fs_xmx077_1_g1),
    .P1(gp_fs_xmx077_1_p1), .G2(gp_fs_xmx077_1_g2), .P2(gp_fs_xmx077_1_p2), .G3(gp_fs_xmx077_1_g3),
    .P3(gp_fs_xmx077_1_p3), .P_star(P_star), .C1(C1), .C2(C2), .C3(C3), .G_star(G_star), .C4(B_out));

  // Other names for the same wires on the sheet: A0 = Ai[0]; A1 = Ai[1]; A2 = Ai[2]; A3 = Ai[3]; B0 = Bi[0];
  //   B1 = Bi[1]; B2 = Bi[2]; B3 = Bi[3]; BX = B_in
endmodule

module FS_8bits_unsigned (
  input  [7:0] in_1,
  input  [7:0] in_2,
  output [7:0] S_out,
  output out_4
);

  wire fs_4bits_unsigned_1_g_star, fs_4bits_unsigned_1_p_star, fs_4bits_unsigned_2_g_star,
       fs_4bits_unsigned_2_p_star, n4_bit_carry_ahead_xmx077_1_c1;

  // Probe on in_1
  // Probe on in_2
  FS_4bits_unsigned fs_4bits_unsigned_1 (
    .Ai(in_1[7:4]), .Bi(in_2[7:4]), .B_in(n4_bit_carry_ahead_xmx077_1_c1),
    .P_star(fs_4bits_unsigned_1_p_star), .G_star(fs_4bits_unsigned_1_g_star), .S_out(S_out[7:4]),
    .B_out(out_4));
  FS_4bits_unsigned fs_4bits_unsigned_2 (
    .Ai(in_1[3:0]), .Bi(in_2[3:0]), .B_in(1'b0), .P_star(fs_4bits_unsigned_2_p_star),
    .G_star(fs_4bits_unsigned_2_g_star), .S_out(S_out[3:0]));  // open: B_out
  _4_BIT_CARRY_AHEAD_xmx077 u_4_bit_carry_ahead_xmx077_1 (
    .G0(fs_4bits_unsigned_2_g_star), .P0(fs_4bits_unsigned_2_p_star), .C0(1'b0),
    .G1(fs_4bits_unsigned_1_g_star), .P1(fs_4bits_unsigned_1_p_star), .G2(1'b0), .P2(1'b0), .G3(1'b0),
    .P3(1'b0), .C1(n4_bit_carry_ahead_xmx077_1_c1));  // open: P_star, C2, C3, G_star, C4
  // Probe on S_out

  // Other names for the same wires on the sheet: S_Lo[3:0] = S_out[3:0]; S_Hi[3:0] = S_out[7:4]
endmodule

module FS_8bits_signed (
  input  [7:0] A,
  input  [7:0] B,
  output [7:0] S_A,
  output OF
);

  wire fa_4bits_unsigned_xmx077_1_g, fa_4bits_unsigned_xmx077_1_p, fa_4bits_unsigned_xmx077_2_c3,
       fa_4bits_unsigned_xmx077_2_cf, fa_4bits_unsigned_xmx077_2_g, fa_4bits_unsigned_xmx077_2_p,
       n4_bit_carry_ahead_xmx077_1_c1;
  wire [3:0] B0_3, B4_7;

  FA_4bits_unsigned_xmx077 fa_4bits_unsigned_xmx077_1 (
    .X(A[3:0]), .Y(B0_3), .C_in(1'b1), .G(fa_4bits_unsigned_xmx077_1_g), .P(fa_4bits_unsigned_xmx077_1_p),
    .F(S_A[3:0]));  // open: OF, CF, C3
  FA_4bits_unsigned_xmx077 fa_4bits_unsigned_xmx077_2 (
    .X(A[7:4]), .Y(B4_7), .C_in(n4_bit_carry_ahead_xmx077_1_c1), .CF(fa_4bits_unsigned_xmx077_2_cf),
    .G(fa_4bits_unsigned_xmx077_2_g), .P(fa_4bits_unsigned_xmx077_2_p), .F(S_A[7:4]),
    .C3(fa_4bits_unsigned_xmx077_2_c3));  // open: OF
  xor xor_1 (OF, fa_4bits_unsigned_xmx077_2_cf, fa_4bits_unsigned_xmx077_2_c3);
  _4_BIT_CARRY_AHEAD_xmx077 u_4_bit_carry_ahead_xmx077_1 (
    .G0(fa_4bits_unsigned_xmx077_1_g), .P0(fa_4bits_unsigned_xmx077_1_p), .C0(1'b1),
    .G1(fa_4bits_unsigned_xmx077_2_g), .P1(fa_4bits_unsigned_xmx077_2_p), .G2(1'b0), .P2(1'b0), .G3(1'b0),
    .P3(1'b0), .C1(n4_bit_carry_ahead_xmx077_1_c1));  // open: P_star, C2, C3, G_star, C4
  // Probe on S_A
  // Probe on A
  // Probe on B
  assign {B4_7, B0_3} = ~B;  // NOT_Gate not_1, 8 bits wide

  // Other names for the same wires on the sheet: A0_3[3:0] = A[3:0]; A4_7[3:0] = A[7:4]; lo[3:0] = S_A[3:0];
  //   hi[3:0] = S_A[7:4]
endmodule

module ALU_8bit_xmx077 (
  input  [7:0] A,
  input  [7:0] B,
  input  [3:0] in_3,
  output [7:0] out_4,
  output out_5,
  output out_6,
  output out_7
);

  wire CF_minus, CF_plus, OF_minus, OF_plus;
  wire [7:0] F0, F1, F2, F3, F4, F5, F6, F7;

  MULTIPLY_4bits_xmx077 multiply_4bits_xmx077_1 (.B(B[3:0]), .A(A[3:0]), .F(F4));
  FS_8bits_signed fs_8bits_signed_1 (.A(A), .B(B), .S_A(F3), .OF(OF_minus));
  FA_8bits_signed_xmx077 fa_8bits_signed_xmx077_1 (.A(A), .B(B), .S_A(F2), .OF(OF_plus));
  FS_8bits_unsigned fs_8bits_unsigned_1 (.in_1(A), .in_2(B), .S_out(F1), .out_4(CF_minus));
  FA_8bits_unsigned_xmx077 fa_8bits_unsigned_xmx077_1 (.A(A), .B(B), .S_A(F0), .out_5(CF_plus));  // open: out_4
  assign F5 = A ^ B;  // XOR_Gate xor_1, 8 bits wide
  assign F6 = A & B;  // AND_Gate and_1, 8 bits wide
  assign F7 = A | B;  // OR_Gate or_1, 8 bits wide
  Multiplexer #(.select(4), .width(8), .enable("false")) multiplexer_1 (
    .in0(A), .in1(F3), .in2(F2), .in3(F1), .in4(F0), .in5(F4), .in6(F5), .in7(F6), .in8(F7), .in9({8{1'b0}}),
    .in10({8{1'b0}}), .in11({8{1'b0}}), .in12({8{1'b0}}), .in13({8{1'b0}}), .in14({8{1'b0}}),
    .in15({8{1'b0}}), .out(out_4), .sel(in_3));
  // Probe on out_4
  Multiplexer #(.select(4), .enable("false")) multiplexer_2 (
    .in0(1'b0), .in1(CF_plus), .in2(CF_minus), .in3(1'b0), .in4(1'b0), .in5(1'b0), .in6(1'b0), .in7(1'b0),
    .in8(1'b0), .in9(1'b0), .in10(1'b0), .in11(1'b0), .in12(1'b0), .in13(1'b0), .in14(1'b0), .in15(1'b0),
    .out(out_6), .sel(in_3));
  Multiplexer #(.select(4), .enable("false")) multiplexer_3 (
    .in0(1'b0), .in1(1'b0), .in2(1'b0), .in3(OF_plus), .in4(OF_minus), .in5(1'b0), .in6(1'b0), .in7(1'b0),
    .in8(1'b0), .in9(1'b0), .in10(1'b0), .in11(1'b0), .in12(1'b0), .in13(1'b0), .in14(1'b0), .in15(1'b0),
    .out(out_7), .sel(in_3));
  nor nor_1 (out_5, out_4[0], out_4[1], out_4[2], out_4[3], out_4[4], out_4[5], out_4[6], out_4[7]);

  // Other names for the same wires on the sheet: A4[3:0] = A[3:0]; ALU_OP[3:0] = in_3; B4[3:0] = B[3:0]; CF = out_7;
  //   F_out[7:0] = out_4; OF = out_6; ZF = out_5
endmodule
