// Logisim project CPU_8bits.circ as structural Verilog: 4 circuits, main circuit main
module main (
  input  INTQ,
  input  EN,
  input  Start,
  input  RST,
  input  [7:0] Pre_uAddress,
  input  [7:0] PreData
);

  wire alu_8bit_xmx077_1_out_5, alu_8bit_xmx077_1_out_7, ALU_BUS, AR, CF, clock_1_out, CS_RAM, CS_ROM, EXEC,
       fetch, LDAR2, LDDR1, LDDR2, LDER, LDPC, LDR4, M4, not_1_out, P0, P1, P2, P3, PC_1, PC_ADD, R_RAM,
       RF_BUS, T1, T2, T3, T4, W_RAM, W_RF, ZF;
  wire [3:0] A, ALU_OP;
  wire [5:0] next_uA, uA;
  wire [7:0] A0, AR0, AR2_out, B0, bit_extender_1_out, controlled_buffer_3_out, CPC, DBUS, DR1_out_5, DR2,
       ER_out_5, IR_in, multiplexer_1_out, PC, pc_add_1_s_out, R0, R1, R2, R3, R4_out_5, S0;
  wire [7:4] IR;
  wire [31:0] uIns;

  Clock clock_1 (.out(clock_1_out));
  DR u_DR2 (.in_1(A0), .LDDR(LDDR1), .CLK(T4), .out_5(DR2), .CLEAR(RST));
  Timing_sequence_main main_1 (
    .T4(T4), .T1(T1), .T2(T2), .T3(T3), .clk(clock_1_out), .CLR(not_1_out), .EN(EN), .Start(Start));  // open: Stop
  not not_1 (not_1_out, RST);
  ALU_8bit_xmx077 alu_8bit_xmx077_1 (
    .A(DR2), .B(DR1_out_5), .in_3(ALU_OP), .out_4(S0), .out_5(alu_8bit_xmx077_1_out_5),
    .out_7(alu_8bit_xmx077_1_out_7));  // open: out_6
  RF_4_main main_2 (
    .D_in(ER_out_5), .clk(T4), .A_out(A0), .RS(A[3:2]), .B_out(B0), .RD(A[1:0]), .reset(RST), .Write(W_RF),
    .WRD(A[1:0]), .R1_o(R1), .R0_o(R0), .R3_o(R3), .R2_o(R2));
  DR ER (.in_1(DBUS), .LDDR(LDER), .CLK(T3), .out_5(ER_out_5), .CLEAR(RST));
  D_Flip_Flop d_ff_1 (
    .clk(T4), .D(alu_8bit_xmx077_1_out_5), .Q(ZF), .preset(1'b0), .en(LDER), .reset(RST));  // open: Qn
  assign DBUS = ALU_BUS ? S0 : 8'bz;  // Controlled_Buffer controlled_buffer_1
  DR DR1 (.in_1(B0), .LDDR(LDDR2), .CLK(T4), .out_5(DR1_out_5), .CLEAR(RST));
  assign DBUS = RF_BUS ? B0 : 8'bz;  // Controlled_Buffer controlled_buffer_2
  uC uc_1 (
    .INTQ(INTQ), .ZF(ZF),
    .uOP_signal({LDR4, LDDR2, LDDR1, RF_BUS, ALU_BUS, LDER, M4, PC_ADD, fetch, LDPC, PC_1, CS_ROM, LDAR2, AR, R_RAM, W_RAM, CS_RAM, W_RF, ALU_OP}),
    .CF(CF), .OP(IR), .clk_T1(T1), .reset(RST), .clk_T4(T4), .Current_UA(uA), .Pre_Data(Pre_uAddress),
    .out_10(P3), .out_11(P2), .out_12(P1), .out_13(P0), .next_uA(next_uA), .uIns(uIns));
  D_Flip_Flop d_ff_2 (
    .clk(T4), .D(alu_8bit_xmx077_1_out_7), .Q(CF), .preset(1'b0), .en(LDER), .reset(RST));  // open: Qn
  or or_1 (EXEC, AR, P1, P3, P0, LDDR2, LDER, W_RAM, LDPC, W_RF);
  // Probe on A0
  // Probe on B0
  // Probe on S0
  LED led_1 (.in(ZF));
  LED led_2 (.in(CF));
  DR AR1 (.in_1(DBUS), .LDDR(AR), .CLK(T2), .out_5(AR0), .CLEAR(RST));
  assign controlled_buffer_3_out = W_RAM ? DBUS : 8'bz;  // Controlled_Buffer controlled_buffer_3
  Register register_1 (.D(PC), .en(fetch), .Q(CPC), .clk(T2), .clr(RST));
  RAM #(.bus("separate")) ram_1 (
    .addr(AR0), .din(controlled_buffer_3_out), .data(DBUS), .str(W_RAM), .sel(CS_RAM), .clk(T3), .ld(R_RAM),
    .clr(RST));
  // Probe on R0
  // Probe on R1
  // Probe on R2
  // Probe on R3
  DR AR2 (.in_1(PC), .LDDR(LDAR2), .CLK(T2), .out_5(AR2_out), .CLEAR(RST));
  PC_Register3_main main_3 (
    .clk_T4(T4), .reset(RST), .PC_in(pc_add_1_s_out), .Preset_data(PreData), .PC_out(PC), .PC_1(PC_1),
    .LDPC(LDPC));
  ROM rom_1 (.addr(AR2_out), .data(IR_in), .sel(CS_ROM));
  PC_ADD pc_add_1 (.Din_1(R4_out_5), .Din_2(PC), .PC_ADD(PC_ADD), .S_out(pc_add_1_s_out));
  DR R4 (.in_1(multiplexer_1_out), .LDDR(LDR4), .CLK(T2), .out_5(R4_out_5), .CLEAR(RST));
  Multiplexer #(.width(8), .enable("false")) multiplexer_1 (
    .in0(DBUS), .in1(bit_extender_1_out), .out(multiplexer_1_out), .sel(M4));
  assign bit_extender_1_out = {{4{1'b0}}, A};  // Bit_Extender bit_extender_1
  LED led_3 (.in(fetch));
  LED led_4 (.in(EXEC));
  // Probe on CPC
  // Probe on PC
  // Probe on {IR, A}
  // Probe on AR0
  // Probe on DR2
  DR u_IR (.in_1(IR_in), .LDDR(fetch), .CLK(T3), .out_5({IR, A}), .CLEAR(RST));
  LED led_5 (.in(M4));
  LED led_6 (.in(AR));
  // Probe on uA
  // Probe on uIns
  // Probe on next_uA
  // Probe on A[1:0]
  // Probe on A[3:2]

  // Other names for the same wires on the sheet: LDAR1 = AR; LDIR = fetch; IR[3:0] = A; RD[1:0] = A[1:0];
  //   WRD[1:0] = A[1:0]; RS[1:0] = A[3:2]; OP[3:0] = IR; reset = RST

  // Notes on the sheet:
  //   20162180077 谢萌新
  //   contents of rom_1 (hex, n*v repeats v):
  //   3e 31 50 51 d7 d6 55 e2 f2 47 88 db 84
endmodule

module DR (
  input  [7:0] in_1,
  input  LDDR,
  input  CLK,
  input  CLEAR,
  output [7:0] out_5
);

  Register register_1 (.D(in_1), .en(LDDR), .Q(out_5), .clk(CLK), .clr(CLEAR));
endmodule

module PC_ADD (
  input  [7:0] Din_1,
  input  [7:0] Din_2,
  input  PC_ADD,
  output [7:0] S_out
);

  wire [7:0] fa_8bits_unsigned_xmx077_1_s_a;

  FA_8bits_unsigned_xmx077 fa_8bits_unsigned_xmx077_1 (
    .A(Din_1), .B(Din_2), .S_A(fa_8bits_unsigned_xmx077_1_s_a));  // open: out_4, out_5
  Multiplexer #(.width(8), .enable("false")) multiplexer_1 (
    .in0(Din_1), .in1(fa_8bits_unsigned_xmx077_1_s_a), .out(S_out), .sel(PC_ADD));
endmodule

module uC (
  input  INTQ,
  input  ZF,
  input  CF,
  input  [3:0] OP,
  input  clk_T1,
  input  reset,
  input  clk_T4,
  input  [7:0] Pre_Data,
  output [21:0] uOP_signal,
  output out_10,
  output out_11,
  output out_12,
  output out_13,
  output [31:0] uIns,
  output [5:0] next_uA,
  output [5:0] Current_UA
);

  wire and_1_out, and_2_out, and_3_out, and_4_out, and_5_out, and_6_out, and_7_out, and_8_out, and_9_out,
       and_10_out, and_11_out, and_12_out, nor_1_out, not_1_out, not_2_out, not_3_out;
  wire [5:0] register_1_q;
  wire [7:0] bit_extender_1_out, main_1_q_out;

  // Probe on uIns
  ROM #(.addrWidth(6), .dataWidth(32)) rom_1 (.addr(Current_UA), .data(uIns), .sel(1'b1));
  Register #(.width(32)) register_1 (
    .D(uIns), .en(1'b1),
    .Q({uOP_signal, out_10, out_11, out_12, out_13, register_1_q[5], next_uA[4], register_1_q[3:0]}),
    .clk(clk_T1), .clr(reset));
  not not_1 (not_1_out, ZF);
  nor nor_1 (nor_1_out, out_10, out_12, out_13);
  not not_2 (not_2_out, out_11);
  and and_1 (and_1_out, not_1_out, out_10);
  and and_2 (and_2_out, CF, out_13);
  and and_3 (and_3_out, nor_1_out, register_1_q[5]);
  and and_4 (and_4_out, out_12, INTQ);
  and and_5 (and_5_out, not_2_out, register_1_q[0]);
  and and_6 (and_6_out, out_11, OP[0]);
  and and_7 (and_7_out, not_2_out, register_1_q[1]);
  and and_8 (and_8_out, out_11, OP[1]);
  and and_9 (and_9_out, not_2_out, register_1_q[2]);
  and and_10 (and_10_out, out_11, OP[2]);
  and and_11 (and_11_out, not_2_out, register_1_q[3]);
  and and_12 (and_12_out, out_11, OP[3]);
  or or_1 (next_uA[5], and_1_out, and_2_out, and_3_out, and_4_out);
  or or_2 (next_uA[0], and_5_out, and_6_out);
  or or_3 (next_uA[1], and_7_out, and_8_out);
  or or_4 (next_uA[2], and_9_out, and_10_out);
  or or_5 (next_uA[3], and_11_out, and_12_out);
  assign bit_extender_1_out = {{2{1'b0}}, next_uA};  // Bit_Extender bit_extender_1
  uAddressR_main main_1 (
    .clk_T4(clk_T4), .reset(reset), .D_in(bit_extender_1_out), .Preset_data(Pre_Data), .Q_out(main_1_q_out),
    .Load(not_3_out));
  not not_3 (not_3_out, reset);
  Bit_Extender #(.out_width(6)) bit_extender_2 (.in(main_1_q_out), .out(Current_UA));

  // Other names for the same wires on the sheet: P0 = out_13; P1 = out_12; P2 = out_11; P3 = out_10; T1 = clk_T1;
  //   T4 = clk_T4; uA_in[5:0] = Current_UA

  // Notes on the sheet:
  //   contents of rom_1 (hex, n*v repeats v):
  //   0 1 2 3 4 b80110 6 7 8 9 a b c d e 80005 6000003b 6000003a 60000039 60000038 5004002b 10040035
  //   60000034 60000033 9040000f 4f 20f1a 1b 1c 60000031 60000030 20f 20 21 22 23 24 25 26 27 28 29 400f
  //   801800f 2c 2d 2e 2f c000c2a c00102a 32 c00182a c001c2a 402802a 36 37 c00202a c00142a c00042a c00082a
  //   3c 3d 3e 3f
endmodule
