// Logisim project PC_Register3.circ as structural Verilog: 1 circuit, main circuit main
module main (
  input  clk_T4,
  input  reset,
  input  PC_1,
  input  [7:0] PC_in,
  input  [7:0] Preset_data,
  input  LDPC,
  output [7:0] PC_out
);

  wire controlled_buffer_1_out, controlled_buffer_2_out, controlled_buffer_3_out, controlled_buffer_4_out,
       controlled_buffer_5_out, controlled_buffer_6_out, controlled_buffer_7_out, controlled_buffer_8_out,
       controlled_buffer_9_out, controlled_buffer_10_out, controlled_buffer_11_out, controlled_buffer_12_out,
       controlled_buffer_13_out, controlled_buffer_14_out, controlled_buffer_15_out,
       controlled_buffer_16_out, D0, D1, D2, D3, D4, D5, D6, D7, not_1_out, not_2_out, not_3_out, not_4_out,
       not_5_out, not_6_out, not_7_out, not_8_out, or_1_out;
  wire [7:0] adder_1_out;

  // Probe on PC_in
  // Probe on PC_out
  or or_1 (or_1_out, PC_1, LDPC);
  Multiplexer #(.width(8), .enable("false")) multiplexer_1 (
    .in0(adder_1_out), .in1(PC_in), .out({D7, D6, D5, D4, D3, D2, D1, D0}), .sel(LDPC));
  // Probe on {D7, D6, D5, D4, D3, D2, D1, D0}
  D_Flip_Flop d_ff_1 (
    .clk(clk_T4), .D(D7), .Q(PC_out[7]), .preset(controlled_buffer_1_out), .en(or_1_out),
    .reset(controlled_buffer_2_out));  // open: Qn
  assign controlled_buffer_1_out = reset ? Preset_data[7] : 1'bz;  // Controlled_Buffer controlled_buffer_1
  assign controlled_buffer_2_out = reset ? not_1_out : 1'bz;  // Controlled_Buffer controlled_buffer_2
  not not_1 (not_1_out, Preset_data[7]);
  Adder adder_1 (.a(PC_out), .b(8'h1), .out(adder_1_out));  // open: cin, cout
  assign controlled_buffer_3_out = reset ? Preset_data[6] : 1'bz;  // Controlled_Buffer controlled_buffer_3
  not not_2 (not_2_out, Preset_data[6]);
  assign controlled_buffer_4_out = reset ? not_2_out : 1'bz;  // Controlled_Buffer controlled_buffer_4
  D_Flip_Flop d_ff_2 (
    .clk(clk_T4), .D(D6), .Q(PC_out[6]), .preset(controlled_buffer_3_out), .en(or_1_out),
    .reset(controlled_buffer_4_out));  // open: Qn
  // Probe on Preset_data
  // Probe on adder_1_out
  assign controlled_buffer_5_out = reset ? Preset_data[5] : 1'bz;  // Controlled_Buffer controlled_buffer_5
  assign controlled_buffer_6_out = reset ? not_3_out : 1'bz;  // Controlled_Buffer controlled_buffer_6
  not not_3 (not_3_out, Preset_data[5]);
  D_Flip_Flop d_ff_3 (
    .clk(clk_T4), .D(D5), .Q(PC_out[5]), .preset(controlled_buffer_5_out), .en(or_1_out),
    .reset(controlled_buffer_6_out));  // open: Qn
  assign controlled_buffer_7_out = reset ? Preset_data[4] : 1'bz;  // Controlled_Buffer controlled_buffer_7
  not not_4 (not_4_out, Preset_data[4]);
  assign controlled_buffer_8_out = reset ? not_4_out : 1'bz;  // Controlled_Buffer controlled_buffer_8
  D_Flip_Flop d_ff_4 (
    .clk(clk_T4), .D(D4), .Q(PC_out[4]), .preset(controlled_buffer_7_out), .en(or_1_out),
    .reset(controlled_buffer_8_out));  // open: Qn
  assign controlled_buffer_9_out = reset ? Preset_data[3] : 1'bz;  // Controlled_Buffer controlled_buffer_9
  assign controlled_buffer_10_out = reset ? not_5_out : 1'bz;  // Controlled_Buffer controlled_buffer_10
  not not_5 (not_5_out, Preset_data[3]);
  D_Flip_Flop d_ff_5 (
    .clk(clk_T4), .D(D3), .Q(PC_out[3]), .preset(controlled_buffer_9_out), .en(or_1_out),
    .reset(controlled_buffer_10_out));  // open: Qn
  not not_6 (not_6_out, Preset_data[2]);
  D_Flip_Flop d_ff_6 (
    .clk(clk_T4), .D(D2), .Q(PC_out[2]), .preset(controlled_buffer_11_out), .en(or_1_out),
    .reset(controlled_buffer_12_out));  // open: Qn
  assign controlled_buffer_11_out = reset ? Preset_data[2] : 1'bz;  // Controlled_Buffer controlled_buffer_11
  assign controlled_buffer_12_out = reset ? not_6_out : 1'bz;  // Controlled_Buffer controlled_buffer_12
  not not_7 (not_7_out, Preset_data[1]);
  D_Flip_Flop d_ff_7 (
    .clk(clk_T4), .D(D1), .Q(PC_out[1]), .preset(controlled_buffer_13_out), .en(or_1_out),
    .reset(controlled_buffer_14_out));  // open: Qn
  assign controlled_buffer_13_out = reset ? Preset_data[1] : 1'bz;  // Controlled_Buffer controlled_buffer_13
  assign controlled_buffer_14_out = reset ? not_7_out : 1'bz;  // Controlled_Buffer controlled_buffer_14
  not not_8 (not_8_out, Preset_data[0]);
  D_Flip_Flop d_ff_8 (
    .clk(clk_T4), .D(D0), .Q(PC_out[0]), .preset(controlled_buffer_15_out), .en(or_1_out),
    .reset(controlled_buffer_16_out));  // open: Qn
  assign controlled_buffer_15_out = reset ? Preset_data[0] : 1'bz;  // Controlled_Buffer controlled_buffer_15
  assign controlled_buffer_16_out = reset ? not_8_out : 1'bz;  // Controlled_Buffer controlled_buffer_16

  // Other names for the same wires on the sheet: Q0 = PC_out[0]; Q1 = PC_out[1]; Q2 = PC_out[2]; Q3 = PC_out[3];
  //   Q4 = PC_out[4]; Q5 = PC_out[5]; Q6 = PC_out[6]; Q7 = PC_out[7]; Preset_0 = Preset_data[0];
  //   Preset_1 = Preset_data[1]; Preset_2 = Preset_data[2]; Preset_3 = Preset_data[3]; Preset_4 = Preset_data[4];
  //   Preset_5 = Preset_data[5]; Preset_6 = Preset_data[6]; Preset_7 = Preset_data[7]

  // Notes on the sheet:
  //   reset=1时，预置入初始化PC数据，clk_T4上升沿到达后，PC执行递增加1，或者装载D_In的输入数据
  //   预置的数据怎么清零？
endmodule
