// Logisim project RAM_8bits.circ as structural Verilog: 1 circuit, main circuit main
// D_in
module main (
  input  [7:0] Add_in,
  input  [7:0] D_in,
  input  Write,
  input  CLR,
  input  cs,
  input  Read,
  input  clk,
  output [7:0] D_out
);

  RAM #(.bus("separate")) ram_1 (
    .addr(Add_in), .din(D_in), .data(D_out), .str(Write), .sel(cs), .clk(clk), .ld(Read), .clr(CLR));
endmodule
