// Logisim project RF_4.circ as structural Verilog: 1 circuit, main circuit main
module main (
  input  [7:0] D_in,
  input  clk,
  input  [1:0] RS,
  input  [1:0] RD,
  input  reset,
  input  Write,
  input  [1:0] WRD,
  output [7:0] R1_o,
  output [7:0] R0_o,
  output [7:0] A_out,
  output [7:0] B_out,
  output [7:0] R3_o,
  output [7:0] R2_o
);

  wire decoder_1_out0, decoder_1_out1, decoder_1_out2, decoder_1_out3;

  Decoder #(.select(2), .disabled(0)) decoder_1 (
    .out0(decoder_1_out0), .out1(decoder_1_out1), .out2(decoder_1_out2), .out3(decoder_1_out3), .sel(WRD),
    .en(Write));
  Register R0 (.D(D_in), .en(decoder_1_out0), .Q(R0_o), .clk(clk), .clr(reset));
  Register R1 (.D(D_in), .en(decoder_1_out1), .Q(R1_o), .clk(clk), .clr(reset));
  Register R2 (.D(D_in), .en(decoder_1_out2), .Q(R2_o), .clk(clk), .clr(reset));
  Register R3 (.D(D_in), .en(decoder_1_out3), .Q(R3_o), .clk(clk), .clr(reset));
  Multiplexer #(.select(2), .width(8), .enable("false")) multiplexer_1 (
    .in0(R0_o), .in1(R1_o), .in2(R2_o), .in3(R3_o), .out(A_out), .sel(RS));
  Multiplexer #(.select(2), .width(8), .enable("false")) multiplexer_2 (
    .in0(R0_o), .in1(R1_o), .in2(R2_o), .in3(R3_o), .out(B_out), .sel(RD));
endmodule
