// Logisim project Timing_sequence.circ as structural Verilog: 1 circuit, main circuit main
module main (
  input  Start,
  input  Stop,
  input  CLR,
  input  EN,
  input  clk,
  output T4,
  output T1,
  output T2,
  output T3
);

  wire _2_out, and_2_out, and_4_out, and_6_out, C1_q, C2_q, C2_qn, C3_q, C3_qn, C4_q, C4_qn, d_ff_1_q,
       nand_1_out, nand_2_out, nand_3_out, nand_4_out, not_1_out, not_2_out, not_3_out, not_4_out, not_5_out,
       not_6_out;

  nand _2 (_2_out, not_1_out, C4_qn);
  not not_1 (not_1_out, clk);
  and and_1 (T4, nand_1_out, d_ff_1_q);
  nand nand_1 (nand_1_out, C1_q, C1_q);
  D_Flip_Flop C1 (.clk(_2_out), .D(1'b1), .Q(C1_q), .en(EN), .reset(and_2_out));  // open: Qn, preset
  and and_2 (and_2_out, clk, C4_q);
  not not_2 (not_2_out, CLR);
  and and_3 (T1, and_4_out, d_ff_1_q);
  and and_4 (and_4_out, C1_q, C2_qn);
  D_Flip_Flop C4 (.clk(not_1_out), .D(C3_q), .Q(C4_q), .Qn(C4_qn), .preset(not_2_out), .en(EN));  // open: reset
  and and_5 (T2, and_6_out, d_ff_1_q);
  and and_6 (and_6_out, C2_q, C3_qn);
  D_Flip_Flop C2 (.clk(_2_out), .D(C1_q), .Q(C2_q), .Qn(C2_qn), .en(EN), .reset(and_2_out));  // open: preset
  and and_7 (T3, nand_2_out, d_ff_1_q);
  nand nand_2 (nand_2_out, C3_qn, C3_qn);
  D_Flip_Flop C3 (.clk(_2_out), .D(C2_q), .Q(C3_q), .Qn(C3_qn), .en(EN), .reset(and_2_out));  // open: preset
  not not_3 (not_3_out, nand_1_out);
  nand nand_3 (nand_3_out, not_4_out, nand_4_out);
  not not_4 (not_4_out, Start);
  D_Flip_Flop d_ff_1 (.clk(not_3_out), .D(nand_3_out), .Q(d_ff_1_q), .reset(not_6_out));  // open: Qn, preset, en
  nand nand_4 (nand_4_out, nand_3_out, not_5_out, CLR);
  not not_5 (not_5_out, Stop);
  not not_6 (not_6_out, CLR);

  // Notes on the sheet:
  //   当Stop有效时，也只有当T4下降沿到达后，才进入停机状态——脉冲输出全部为0
  //   EN=1时允许输出脉冲，否则暂停输出，当EN再次有效后，接着继续输出脉冲
  //   Start和Stop都是高电平有效，两个信号不同同时有效，当Start有效，且T4下降沿到达后，才会启动输出脉冲，T1开始输出
  //   CLR=0有效，对脉冲电路进行初始化，但是电路不能进行脉冲输出，再次把CLR=1后，就可以工作了
endmodule
