// Logisim project uAddressR.circ as structural Verilog: 1 circuit, main circuit main
module main (
  input  clk_T4,
  input  reset,
  input  Load,
  input  [7:0] D_in,
  input  [7:0] Preset_data,
  output [7:0] Q_out
);

  wire controlled_buffer_1_out, controlled_buffer_2_out, controlled_buffer_3_out, controlled_buffer_4_out,
       controlled_buffer_5_out, controlled_buffer_6_out, controlled_buffer_7_out, controlled_buffer_8_out,
       controlled_buffer_9_out, controlled_buffer_10_out, controlled_buffer_11_out, controlled_buffer_12_out,
       controlled_buffer_13_out, controlled_buffer_14_out, controlled_buffer_15_out,
       controlled_buffer_16_out, not_1_out, not_2_out, not_3_out, not_4_out, not_5_out, not_6_out, not_7_out,
       not_8_out;

  // Probe on D_in
  // Probe on Q_out
  D_Flip_Flop d_ff_1 (
    .clk(clk_T4), .D(D_in[7]), .Q(Q_out[7]), .preset(controlled_buffer_1_out), .en(Load),
    .reset(controlled_buffer_2_out));  // open: Qn
  assign controlled_buffer_1_out = reset ? Preset_data[7] : 1'bz;  // Controlled_Buffer controlled_buffer_1
  not not_1 (not_1_out, Preset_data[7]);
  assign controlled_buffer_2_out = reset ? not_1_out : 1'bz;  // Controlled_Buffer controlled_buffer_2
  assign controlled_buffer_3_out = reset ? Preset_data[6] : 1'bz;  // Controlled_Buffer controlled_buffer_3
  not not_2 (not_2_out, Preset_data[6]);
  assign controlled_buffer_4_out = reset ? not_2_out : 1'bz;  // Controlled_Buffer controlled_buffer_4
  D_Flip_Flop d_ff_2 (
    .clk(clk_T4), .D(D_in[6]), .Q(Q_out[6]), .preset(controlled_buffer_3_out), .en(Load),
    .reset(controlled_buffer_4_out));  // open: Qn
  // Probe on Preset_data
  assign controlled_buffer_5_out = reset ? Preset_data[5] : 1'bz;  // Controlled_Buffer controlled_buffer_5
  assign controlled_buffer_6_out = reset ? not_3_out : 1'bz;  // Controlled_Buffer controlled_buffer_6
  not not_3 (not_3_out, Preset_data[5]);
  D_Flip_Flop d_ff_3 (
    .clk(clk_T4), .D(D_in[5]), .Q(Q_out[5]), .preset(controlled_buffer_5_out), .en(Load),
    .reset(controlled_buffer_6_out));  // open: Qn
  assign controlled_buffer_7_out = reset ? Preset_data[4] : 1'bz;  // Controlled_Buffer controlled_buffer_7
  assign controlled_buffer_8_out = reset ? not_4_out : 1'bz;  // Controlled_Buffer controlled_buffer_8
  not not_4 (not_4_out, Preset_data[4]);
  D_Flip_Flop d_ff_4 (
    .clk(clk_T4), .D(D_in[4]), .Q(Q_out[4]), .preset(controlled_buffer_7_out), .en(Load),
    .reset(controlled_buffer_8_out));  // open: Qn
  assign controlled_buffer_9_out = reset ? Preset_data[3] : 1'bz;  // Controlled_Buffer controlled_buffer_9
  assign controlled_buffer_10_out = reset ? not_5_out : 1'bz;  // Controlled_Buffer controlled_buffer_10
  not not_5 (not_5_out, Preset_data[3]);
  D_Flip_Flop d_ff_5 (
    .clk(clk_T4), .D(D_in[3]), .Q(Q_out[3]), .preset(controlled_buffer_9_out), .en(Load),
    .reset(controlled_buffer_10_out));  // open: Qn
  not not_6 (not_6_out, Preset_data[2]);
  D_Flip_Flop d_ff_6 (
    .clk(clk_T4), .D(D_in[2]), .Q(Q_out[2]), .preset(controlled_buffer_11_out), .en(Load),
    .reset(controlled_buffer_12_out));  // open: Qn
  assign controlled_buffer_11_out = reset ? Preset_data[2] : 1'bz;  // Controlled_Buffer controlled_buffer_11
  assign controlled_buffer_12_out = reset ? not_6_out : 1'bz;  // Controlled_Buffer controlled_buffer_12
  not not_7 (not_7_out, Preset_data[1]);
  D_Flip_Flop d_ff_7 (
    .clk(clk_T4), .D(D_in[1]), .Q(Q_out[1]), .preset(controlled_buffer_13_out), .en(Load),
    .reset(controlled_buffer_14_out));  // open: Qn
  assign controlled_buffer_13_out = reset ? Preset_data[1] : 1'bz;  // Controlled_Buffer controlled_buffer_13
  assign controlled_buffer_14_out = reset ? not_7_out : 1'bz;  // Controlled_Buffer controlled_buffer_14
  not not_8 (not_8_out, Preset_data[0]);
  D_Flip_Flop d_ff_8 (
    .clk(clk_T4), .D(D_in[0]), .Q(Q_out[0]), .preset(controlled_buffer_15_out), .en(Load),
    .reset(controlled_buffer_16_out));  // open: Qn
  assign controlled_buffer_15_out = reset ? Preset_data[0] : 1'bz;  // Controlled_Buffer controlled_buffer_15
  assign controlled_buffer_16_out = reset ? not_8_out : 1'bz;  // Controlled_Buffer controlled_buffer_16

  // Other names for the same wires on the sheet: D0 = D_in[0]; D1 = D_in[1]; D2 = D_in[2]; D3 = D_in[3]; D4 = D_in[4];
  //   D5 = D_in[5]; D6 = D_in[6]; D7 = D_in[7]; Preset_0 = Preset_data[0]; Preset_1 = Preset_data[1];
  //   Preset_2 = Preset_data[2]; Preset_3 = Preset_data[3]; Preset_4 = Preset_data[4]; Preset_5 = Preset_data[5];
  //   Preset_6 = Preset_data[6]; Preset_7 = Preset_data[7]; Q0 = Q_out[0]; Q1 = Q_out[1]; Q2 = Q_out[2];
  //   Q3 = Q_out[3]; Q4 = Q_out[4]; Q5 = Q_out[5]; Q6 = Q_out[6]; Q7 = Q_out[7]

  // Notes on the sheet:
  //   reset=1时，预置入初始化PC数据，clk_T4上升沿到达后，装载D_In的输入数据
  //   预置的数据怎么清零？
endmodule
